# Fritzing sketch ESP32 Version Final (12v DC Motor Version)  (saved by Fritzing 0.9.3b)
breadboards: 1

parts:
  DHT1 = Humidity and Temperature Sensor DHT11
  R1 = PHOTOCELL [package=photocell]
  S1 = Pushbutton [package="[THT]"]
  LED1 = LED - 3mm [color="Green (570nm)" package="3 mm [THT]"]
  LED2 = LED - 3mm [color="Red (633nm)" package="3 mm [THT]"]
  S2 = Pushbutton [package="[THT]"]
  S3 = Pushbutton [package="[THT]"]
  R2 = Resistor [tolerance=±5% resistance=10k package="2512 [SMD]"]
  R3 = Resistor [tolerance=±5% resistance=10k package="2512 [SMD]"]
  R4 = Resistor [tolerance=±5% resistance=220 package="2512 [SMD]"]
  R5 = Resistor [tolerance=±5% resistance=220 package="2512 [SMD]"]
  R6 = Resistor [tolerance=±5% resistance=10k package="2512 [SMD]"]  # not connected
  R7 = Resistor [tolerance=±5% resistance=10k package="2512 [SMD]"]
  S4 = D2F-FL Omron Snap Action Limit Switch with Level
  S5 = D2F-FL Omron Snap Action Limit Switch with Level
  HC-SR04_Sensor_1 = HC-SR04 Ultrasonic Distance Sensor
  R8 = Resistor [tolerance=±5% resistance=10k package="2512 [SMD]"]
  R9 = Resistor [tolerance=±5% resistance=10k package="2512 [SMD]"]
  R10 = Resistor [tolerance=±5% resistance=10k package="2512 [SMD]"]
  U1 = ESP32-38PinWide [part_number=ESP32-38PinWide]
  Mod1 = L298N DC motor driver
  M1 = DC Motor
  C1 = Capacitor [package=cap-pth-small2]
  BAT1 = Battery Holders [package=lipo-1100mAh]

nets:
  VCC: DHT1.Vcc, S1.Pin_3, S1.Pin_4, S2.Pin_3, S2.Pin_4, S3.Pin_3, S3.Pin_4, R2.Pin_0, R3.Pin_0, R7.Pin_0, HC-SR04_Sensor_1.VCC, U1.3.3
  N1: DHT1.Data-signal, R2.Pin_1, U1.GPIO33
  GND: DHT1.GND_2, R1.P$2, R4.Pin_0, R5.Pin_0, S4.Pin_1, S5.Pin_1, HC-SR04_Sensor_1.GND, R8.Pin_1, R9.Pin_1, R10.Pin_1, U1.GND
  N2: R1.P$1, R3.Pin_1, U1.GPIO32
  N3: S1.Pin_1, S1.Pin_2, R8.Pin_0, U1.GPIO25
  N4: LED1.cathode, R5.Pin_1
  N5: LED1.anode, U1.GPIO17
  N6: LED2.cathode, R4.Pin_1
  N7: LED2.anode, U1.GPIO16
  N8: S2.Pin_1, S2.Pin_2, R9.Pin_0, U1.GPIO26
  N9: S3.Pin_1, S3.Pin_2, R10.Pin_0, U1.GPIO27
  N10: R7.Pin_1, S4.Pin_2, U1.GPIO35
  N11: S5.Pin_2, U1.GPIO34
  N12: HC-SR04_Sensor_1.TRIG, U1.GPIO13
  N13: HC-SR04_Sensor_1.ECHO, U1.GPIO14
  N14: U1.GPIO2, Mod1.IN2
  N15: U1.GPIO0, Mod1.IN1
  N16: U1.GPIO4, Mod1.ENA
  N17: Mod1.OUT1, M1.pin_2, C1.2
  N18: Mod1.OUT2, M1.pin_1, C1.1
  N19: Mod1.12V, Mod1.5V-ENA-JMP-I, BAT1.+
  N20: Mod1.GND, BAT1.-

notes:
  12V Battery
  40Ah

custom parts:
  Humidity and Temperature Sensor DHT11: Digital relative humidity & temperature sensor DHT11
  D2F-FL Omron Snap Action Limit Switch with Level: Snap action switch with stainless steel lever.
  ESP32-38PinWide: Generic 38-Pin ESP32 with wide format (only access to one side of pins on a breadboard) based on Stephen Lilley's HiLetgo ESP-WROOM-32 ESP32 ESP-32S Development Board.
  L298N DC motor driver: 2x DC motor driver with 78M05 positive voltage regulator (7..35 V) L298N: max 46 V, 2 A Set 5 V Enable jumper to enable 5 V regultor (needed for the L298N) and +5 V output at screw terminal or supply external +5 V at screw terminal Set ENA and/or ENB to +5 V to enable motor permanently or supply ENA and/or ENB with PWM signal IN1 and IN2 set rotation directory for motor A (OUT1/OUT2) IN2 and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
